// Logisim project bigswitch.circ as structural Verilog: 3 circuits, main circuit main
module main (
  input  [31:0] INPUT,
  input  [31:0] CONTROL,
  input  [4:0] in_3,
  input  in_4
);

  wire clock_1_out, decoder_1_out0, decoder_1_out1, decoder_1_out2, decoder_1_out3, decoder_1_out4,
       decoder_1_out5, decoder_1_out6, decoder_1_out7, decoder_1_out8, decoder_1_out9, decoder_1_out10,
       decoder_1_out11, decoder_1_out12, decoder_1_out13, decoder_1_out14, decoder_1_out15, decoder_1_out16,
       decoder_1_out17, decoder_1_out18, decoder_1_out19, decoder_1_out20, decoder_1_out21, decoder_1_out22,
       decoder_1_out23, decoder_1_out24, decoder_1_out25, decoder_1_out26, decoder_1_out27, decoder_1_out28,
       decoder_1_out29, decoder_1_out30, decoder_1_out31;

  switch switch_1 (.CLOCK(clock_1_out), .CONTROL(CONTROL), .ENABLE(decoder_1_out0));  // open: INPUT, CLOCK_2, OUTPUT
  switch switch_2 (.CLOCK(clock_1_out), .CONTROL(CONTROL), .ENABLE(decoder_1_out1));  // open: INPUT, CLOCK_2, OUTPUT
  switch switch_3 (.CLOCK(clock_1_out), .CONTROL(CONTROL), .ENABLE(decoder_1_out2));  // open: INPUT, CLOCK_2, OUTPUT
  switch switch_4 (.CLOCK(clock_1_out), .CONTROL(CONTROL), .ENABLE(decoder_1_out3));  // open: INPUT, CLOCK_2, OUTPUT
  switch switch_5 (.CLOCK(clock_1_out), .CONTROL(CONTROL), .ENABLE(decoder_1_out4));  // open: INPUT, CLOCK_2, OUTPUT
  switch switch_6 (.CLOCK(clock_1_out), .CONTROL(CONTROL), .ENABLE(decoder_1_out5));  // open: INPUT, CLOCK_2, OUTPUT
  switch switch_7 (.CLOCK(clock_1_out), .CONTROL(CONTROL), .ENABLE(decoder_1_out6));  // open: INPUT, CLOCK_2, OUTPUT
  switch switch_8 (.CLOCK(clock_1_out), .CONTROL(CONTROL), .ENABLE(decoder_1_out7));  // open: INPUT, CLOCK_2, OUTPUT
  switch switch_9 (.CLOCK(clock_1_out), .CONTROL(CONTROL), .ENABLE(decoder_1_out8));  // open: INPUT, CLOCK_2, OUTPUT
  switch switch_10 (.CLOCK(clock_1_out), .CONTROL(CONTROL), .ENABLE(decoder_1_out9));  // open: INPUT, CLOCK_2, OUTPUT
  switch switch_11 (.CLOCK(clock_1_out), .CONTROL(CONTROL), .ENABLE(decoder_1_out10));  // open: INPUT, CLOCK_2, OUTPUT
  switch switch_12 (.CLOCK(clock_1_out), .CONTROL(CONTROL), .ENABLE(decoder_1_out11));  // open: INPUT, CLOCK_2, OUTPUT
  Decoder #(.select(5), .disabled(0)) decoder_1 (
    .out0(decoder_1_out0), .out1(decoder_1_out1), .out2(decoder_1_out2), .out3(decoder_1_out3),
    .out4(decoder_1_out4), .out5(decoder_1_out5), .out6(decoder_1_out6), .out7(decoder_1_out7),
    .out8(decoder_1_out8), .out9(decoder_1_out9), .out10(decoder_1_out10), .out11(decoder_1_out11),
    .out12(decoder_1_out12), .out13(decoder_1_out13), .out14(decoder_1_out14), .out15(decoder_1_out15),
    .out16(decoder_1_out16), .out17(decoder_1_out17), .out18(decoder_1_out18), .out19(decoder_1_out19),
    .out20(decoder_1_out20), .out21(decoder_1_out21), .out22(decoder_1_out22), .out23(decoder_1_out23),
    .out24(decoder_1_out24), .out25(decoder_1_out25), .out26(decoder_1_out26), .out27(decoder_1_out27),
    .out28(decoder_1_out28), .out29(decoder_1_out29), .out30(decoder_1_out30), .out31(decoder_1_out31),
    .sel(in_3), .en(in_4));
  Clock clock_1 (.out(clock_1_out));
  switch switch_13 (.CLOCK(clock_1_out), .CONTROL(CONTROL), .ENABLE(decoder_1_out12));  // open: INPUT, CLOCK_2, OUTPUT
  switch switch_14 (.CLOCK(clock_1_out), .CONTROL(CONTROL), .ENABLE(decoder_1_out13));  // open: INPUT, CLOCK_2, OUTPUT
  switch switch_15 (.CLOCK(clock_1_out), .CONTROL(CONTROL), .ENABLE(decoder_1_out14));  // open: INPUT, CLOCK_2, OUTPUT
  switch switch_16 (.CLOCK(clock_1_out), .CONTROL(CONTROL), .ENABLE(decoder_1_out15));  // open: INPUT, CLOCK_2, OUTPUT
  switch switch_17 (.CLOCK(clock_1_out), .CONTROL(CONTROL), .ENABLE(decoder_1_out16));  // open: INPUT, CLOCK_2, OUTPUT
  switch switch_18 (.CLOCK(clock_1_out), .CONTROL(CONTROL), .ENABLE(decoder_1_out17));  // open: INPUT, CLOCK_2, OUTPUT
  switch switch_19 (.CLOCK(clock_1_out), .CONTROL(CONTROL), .ENABLE(decoder_1_out18));  // open: INPUT, CLOCK_2, OUTPUT
  switch switch_20 (.CLOCK(clock_1_out), .CONTROL(CONTROL), .ENABLE(decoder_1_out19));  // open: INPUT, CLOCK_2, OUTPUT
  switch switch_21 (.CLOCK(clock_1_out), .CONTROL(CONTROL), .ENABLE(decoder_1_out20));  // open: INPUT, CLOCK_2, OUTPUT
  switch switch_22 (.CLOCK(clock_1_out), .CONTROL(CONTROL), .ENABLE(decoder_1_out21));  // open: INPUT, CLOCK_2, OUTPUT
  switch switch_23 (.CLOCK(clock_1_out), .CONTROL(CONTROL), .ENABLE(decoder_1_out22));  // open: INPUT, CLOCK_2, OUTPUT
  switch switch_24 (.CLOCK(clock_1_out), .CONTROL(CONTROL), .ENABLE(decoder_1_out23));  // open: INPUT, CLOCK_2, OUTPUT
  switch switch_25 (.CLOCK(clock_1_out), .CONTROL(CONTROL), .ENABLE(decoder_1_out24));  // open: INPUT, CLOCK_2, OUTPUT
  switch switch_26 (.CLOCK(clock_1_out), .CONTROL(CONTROL), .ENABLE(decoder_1_out25));  // open: INPUT, CLOCK_2, OUTPUT
  switch switch_27 (.CLOCK(clock_1_out), .CONTROL(CONTROL), .ENABLE(decoder_1_out26));  // open: INPUT, CLOCK_2, OUTPUT
  switch switch_28 (.CLOCK(clock_1_out), .CONTROL(CONTROL), .ENABLE(decoder_1_out27));  // open: INPUT, CLOCK_2, OUTPUT
  switch switch_29 (.CLOCK(clock_1_out), .CONTROL(CONTROL), .ENABLE(decoder_1_out28));  // open: INPUT, CLOCK_2, OUTPUT
  switch switch_30 (.CLOCK(clock_1_out), .CONTROL(CONTROL), .ENABLE(decoder_1_out29));  // open: INPUT, CLOCK_2, OUTPUT
  switch switch_31 (.CLOCK(clock_1_out), .CONTROL(CONTROL), .ENABLE(decoder_1_out30));  // open: INPUT, CLOCK_2, OUTPUT
  switch switch_32 (.CLOCK(clock_1_out), .CONTROL(CONTROL), .ENABLE(decoder_1_out31));  // open: INPUT, CLOCK_2, OUTPUT
endmodule

module _4s (
  input  DATA,
  input  [3:0] CONTROL,
  output [3:0] out_3
);

  assign out_3[0] = CONTROL[3] ? DATA : 1'bz;  // Controlled_Buffer controlled_buffer_1
  assign out_3[1] = CONTROL[2] ? DATA : 1'bz;  // Controlled_Buffer controlled_buffer_2
  assign out_3[2] = CONTROL[1] ? DATA : 1'bz;  // Controlled_Buffer controlled_buffer_3
  assign out_3[3] = CONTROL[0] ? DATA : 1'bz;  // Controlled_Buffer controlled_buffer_4
endmodule

module switch (
  input  INPUT,
  input  [31:0] CONTROL,
  input  CLOCK,
  input  CLOCK_2,
  input  ENABLE,
  output [31:0] OUTPUT
);

  wire [3:0] register_1_q_2, register_1_q_3, register_1_q_4, register_1_q_5;
  wire [15:0] register_1_q;

  _4s u_4s_1 (.DATA(INPUT), .CONTROL(register_1_q_5), .out_3(OUTPUT[3:0]));
  _4s u_4s_2 (.DATA(INPUT), .CONTROL(register_1_q_4), .out_3(OUTPUT[7:4]));
  _4s u_4s_3 (.DATA(INPUT), .CONTROL(register_1_q_3), .out_3(OUTPUT[11:8]));
  _4s u_4s_4 (.DATA(INPUT), .CONTROL(register_1_q_2), .out_3(OUTPUT[15:12]));
  _4s u_4s_5 (.DATA(INPUT), .CONTROL(register_1_q[15:12]), .out_3(OUTPUT[19:16]));
  Register #(.width(32)) register_1 (
    .D(CONTROL), .en(ENABLE),
    .Q({register_1_q_5, register_1_q_4, register_1_q_3, register_1_q_2, register_1_q}), .clr(CLOCK));  // open: clk
  _4s u_4s_6 (.DATA(INPUT), .CONTROL(register_1_q[11:8]), .out_3(OUTPUT[23:20]));
  _4s u_4s_7 (.DATA(INPUT), .CONTROL(register_1_q[7:4]), .out_3(OUTPUT[27:24]));
  _4s u_4s_8 (.DATA(INPUT), .CONTROL(register_1_q[3:0]), .out_3(OUTPUT[31:28]));

  assign CLOCK_2 = CLOCK;
endmodule
