// Logisim project signal selector.circ as structural Verilog: 1 circuit, main circuit main
module main (
  input  C1,
  input  C2,
  input  C3
);

  wire and_1_out, not_1_out;
  wire [1:0] or_1_out;

  or or_1 (or_1_out[0], C3, C2);
  and and_1 (and_1_out, C1, not_1_out);
  not not_1 (not_1_out, C2);
  or or_2 (or_1_out[1], C3, and_1_out);
  Multiplexer #(.select(2)) multiplexer_1 (.sel(or_1_out));  // open: in0, in1, in2, in3, out, en
endmodule
