// Logisim project mute_solo_discrete.circ as structural Verilog: 1 circuit, main circuit main
module main (
);

  wire button_1_out, button_2_out, button_3_out, controlled_buffer_1_out, nand_1_out, nand_2_out,
       pull_resistor_1_node, t_ff_1_qn, t_ff_2_q, t_ff_2_qn;

  Button button_1 (.out(button_1_out));
  LED #(.active("false")) led_1 (.in(t_ff_1_qn));
  T_Flip_Flop t_ff_1 (.T(button_1_out), .clk(button_1_out), .Qn(t_ff_1_qn));  // open: Q, reset, preset
  Button button_2 (.out(button_2_out));
  Pull_Resistor #(.pull(1)) pull_resistor_1 (.node(pull_resistor_1_node));
  Transistor #(.\type ("n")) transistor_1 (.in(1'b0), .out(pull_resistor_1_node), .gate(button_2_out));
  Button button_3 (.out(button_3_out));
  LED led_2 (.in(t_ff_2_q));
  nand nand_1 (nand_1_out, t_ff_1_qn, pull_resistor_1_node);
  T_Flip_Flop t_ff_2 (.T(button_3_out), .clk(button_3_out), .Q(t_ff_2_q), .Qn(t_ff_2_qn));  // open: reset, preset
  Transistor #(.\type ("n")) transistor_2 (.in(1'b0), .out(pull_resistor_1_node), .gate(t_ff_2_q));
  assign controlled_buffer_1_out = nand_2_out ? 1'b1 : 1'bz;  // Controlled_Buffer controlled_buffer_1
  nand nand_2 (nand_2_out, nand_1_out, t_ff_2_qn);

  // Notes on the sheet:
  //   mute button
  //   muted
  //   external solo
  //   soloed
  //   ~global solo
  //   solo button
  //   signal
endmodule
