// Logisim project mute_solo_logic.circ as structural Verilog: 1 circuit, main circuit main
module main (
);

  wire and_1_out, and_2_out, button_1_out, controlled_buffer_1_out, dipswitch_1_sw1, dipswitch_2_sw1,
       not_1_out, or_1_out, pull_resistor_1_node;

  DipSwitch #(.number(1)) dipswitch_1 (.sw1(dipswitch_1_sw1));
  LED led_1 (.in(and_1_out));
  Button button_1 (.out(button_1_out));
  and and_1 (and_1_out, dipswitch_1_sw1, pull_resistor_1_node);
  Pull_Resistor #(.pull(1)) pull_resistor_1 (.node(pull_resistor_1_node));
  Transistor #(.\type ("n")) transistor_1 (.in(1'b0), .out(pull_resistor_1_node), .gate(button_1_out));
  not not_1 (not_1_out, dipswitch_1_sw1);
  and and_2 (and_2_out, not_1_out, pull_resistor_1_node);
  assign controlled_buffer_1_out = or_1_out ? 1'b1 : 1'bz;  // Controlled_Buffer controlled_buffer_1
  or or_1 (or_1_out, and_2_out, dipswitch_2_sw1);
  DipSwitch #(.number(1)) dipswitch_2 (.sw1(dipswitch_2_sw1));
  LED led_2 (.in(dipswitch_2_sw1));
  Pull_Resistor #(.pull(1)) pull_resistor_2 (.node(pull_resistor_1_node));
  Transistor #(.\type ("n")) transistor_2 (.in(1'b0), .out(pull_resistor_1_node), .gate(dipswitch_2_sw1));

  // Notes on the sheet:
  //   mute button
  //   muted
  //   external solo
  //   ~global solo
  //   solo button
  //   signal
  //   soloed
endmodule
